// Logisim project Processador Completo.circ as structural Verilog: 5 circuits, main circuit main
module main (
  output [31:0] Instruction
);

  wire addi, beq, clk, cu_control_unit_1_beq, cu_control_unit_1_selector_r_i, cu_control_unit_1_sw, lw,
       not_1_out, or_1_out, type_i, type_j, \ula_unidade_lógica_e_aritmetica_1_flag_beq ;
  wire [2:0] multiplexer_6_out, ula_op;
  wire [4:0] multiplexer_1_out, multiplexer_2_out, rd, rs_i, rs_r, rt_i, rt_r, shamt;
  wire [5:3] cu_control_unit_1_funct;
  wire [15:0] imediate, multiplexer_3_out;
  wire [23:0] bit_extender_1_out;
  wire [25:0] cu_control_unit_1_label;
  wire [27:0] bit_extender_2_out, shifter_1_out;
  wire [31:0] adder_1_out, adder_2_out, br_banco_de_registradores_1_br_rs, br_banco_de_registradores_1_br_rt,
       multiplexer_4_out, multiplexer_5_out, multiplexer_7_out, multiplexer_8_out,
       PC___Programing_Counting_q, ram_2_data, shifter_2_out, sinal_Ext_Immediate,
       \ula_unidade_lógica_e_aritmetica_1_data ;

  Register #(.width(32), .Select("low")) PC___Programing_Counting (
    .D(multiplexer_8_out), .Q(PC___Programing_Counting_q), .clk(clk));  // open: en, clr
  Adder #(.width(32)) adder_1 (.a(32'h4), .b(PC___Programing_Counting_q), .out(adder_1_out));  // open: cin, cout
  Multiplexer #(.width(5), .enable("false")) multiplexer_1 (
    .in0(rs_r), .in1(rs_i), .out(multiplexer_1_out), .sel(type_i));
  Multiplexer #(.width(5), .enable("false")) multiplexer_2 (
    .in0(rd), .in1(rt_i), .out(multiplexer_2_out), .sel(type_i));
  Multiplexer #(.width(16), .enable("false")) multiplexer_3 (
    .in0({16{1'b0}}), .in1(imediate), .out(multiplexer_3_out), .sel(or_1_out));
  or or_1 (or_1_out, cu_control_unit_1_sw, lw);
  RAM #(.addrWidth(24), .dataWidth(32), .Select("low")) ram_1 (
    .addr(PC___Programing_Counting_q[25:2]), .data(Instruction));  // open: sel, clk, ld, clr
  assign bit_extender_1_out = {{8{1'b0}}, multiplexer_3_out};  // Bit_Extender bit_extender_1
  not not_1 (not_1_out, type_i);
  assign bit_extender_2_out = {{2{1'b0}}, cu_control_unit_1_label};  // Bit_Extender bit_extender_2
  Multiplexer #(.width(32), .enable("false")) multiplexer_4 (
    .in0(\ula_unidade_lógica_e_aritmetica_1_data ), .in1(ram_2_data), .out(multiplexer_4_out), .sel(lw));
  RAM #(.addrWidth(24), .dataWidth(32), .bus("separate"), .simpleMode("false"), .Select("low")) ram_2 (
    .addr(bit_extender_1_out), .din(br_banco_de_registradores_1_br_rs), .data(ram_2_data), .sel(not_1_out),
    .clk(clk));  // open: str, ld, clr
  Shifter #(.width(28)) shifter_1 (.in(bit_extender_2_out), .\dist (5'b00010), .out(shifter_1_out));
  BR___Banco_de_Registradores br_banco_de_registradores_1 (
    .REG_WRTIE(cu_control_unit_1_selector_r_i), .BR_RS(br_banco_de_registradores_1_br_rs),
    .BR_RT(br_banco_de_registradores_1_br_rt), .DATA(multiplexer_4_out), .in_1(clk), .RS(multiplexer_1_out),
    .RT(rt_r), .RD(multiplexer_2_out));
  CU___Control_Unit cu_control_unit_1 (
    .Instruction(Instruction), .FUNCT({cu_control_unit_1_funct, ula_op}), .SHANT(shamt), .RD_R(rd),
    .RT_R(rt_r), .RS_R(rs_r), .Imediate(imediate), .RT_I(rt_i), .RS_I(rs_i), .Type_I(type_i),
    .Label(cu_control_unit_1_label), .Type_J(type_j), .selector_r_i(cu_control_unit_1_selector_r_i),
    .sw(cu_control_unit_1_sw), .beq(cu_control_unit_1_beq), .lw(lw), .addi(addi));  // open: Type_R
  Multiplexer #(.width(32), .enable("false")) multiplexer_5 (
    .in0(br_banco_de_registradores_1_br_rt), .in1(sinal_Ext_Immediate), .out(multiplexer_5_out), .sel(addi));
  Multiplexer #(.width(3), .enable("false")) multiplexer_6 (
    .in0(ula_op), .in1(3'b000), .out(multiplexer_6_out), .sel(type_i));
  \ULA___Unidade_Lógica_e_Aritmetica  \ula_unidade_lógica_e_aritmetica_1  (
    .BR_RS(br_banco_de_registradores_1_br_rs), .BR_RT(multiplexer_5_out),
    .DATA(\ula_unidade_lógica_e_aritmetica_1_data ), .ULA_OP(multiplexer_6_out),
    .Flag_beq(\ula_unidade_lógica_e_aritmetica_1_flag_beq ), .shamt(shamt));  // open: slt
  Multiplexer #(.width(32), .enable("false")) multiplexer_7 (
    .in0(adder_1_out), .in1({adder_1_out[31:28], shifter_1_out}), .out(multiplexer_7_out), .sel(type_j));
  Multiplexer #(.width(32), .enable("false")) multiplexer_8 (
    .in0(multiplexer_7_out), .in1(adder_2_out), .out(multiplexer_8_out), .sel(beq));
  assign sinal_Ext_Immediate = {{16{1'b0}}, imediate};  // Bit_Extender bit_extender_3
  and and_1 (beq, cu_control_unit_1_beq, \ula_unidade_lógica_e_aritmetica_1_flag_beq );
  Shifter #(.width(32)) shifter_2 (.in(sinal_Ext_Immediate), .\dist (5'b00010), .out(shifter_2_out));
  Clock clock_1 (.out(clk));
  Adder #(.width(32)) adder_2 (.a(adder_1_out), .b(shifter_2_out), .out(adder_2_out));  // open: cin, cout
endmodule

module BR___Banco_de_Registradores (
  input  in_1,
  input  [4:0] RS,
  input  [4:0] RT,
  input  [4:0] RD,
  input  REG_WRTIE,
  input  [31:0] DATA,
  output [31:0] BR_RS,
  output [31:0] BR_RT
);

  wire regd1, regd2, regd3, regd4, regd5, regd6, regd7, regd8, regd9, regd10, regd11, regd12, regd13, regd14,
       regd15, regd16, regd17, regd18, regd19, regd20, regd21, regd22, regd23, regd24, regd25, regd26,
       regd27, regd28, regd29, regd30, regd31, regd32;
  wire [31:0] reg1, reg2, reg3, reg4, reg5, reg6, reg7, reg8, reg9, reg10, reg11, reg12, reg13, reg14, reg15,
       reg16, reg17, reg18, reg19, reg20, reg21, reg22, reg23, reg24, reg25, reg26, reg27, reg28, reg29,
       reg30, reg31, reg32;

  Demultiplexer #(.select(5), .enable("false")) demultiplexer_1 (
    .out0(regd1), .out1(regd2), .out2(regd3), .out3(regd4), .out4(regd5), .out5(regd6), .out6(regd7),
    .out7(regd8), .out8(regd9), .out9(regd10), .out10(regd11), .out11(regd12), .out12(regd13),
    .out13(regd14), .out14(regd15), .out15(regd16), .out16(regd17), .out17(regd18), .out18(regd19),
    .out19(regd20), .out20(regd21), .out21(regd22), .out22(regd23), .out23(regd24), .out24(regd25),
    .out25(regd26), .out26(regd27), .out27(regd28), .out28(regd29), .out29(regd30), .out30(regd31),
    .out31(regd32), .in(REG_WRTIE), .sel(RD));
  Register #(.width(32), .Select("low")) register_1 (.Q(reg1), .clk(in_1));  // open: D, en, clr
  Register #(.width(32), .Select("low")) register_2 (.D(DATA), .en(regd2), .Q(reg2), .clk(in_1));  // open: clr
  Register #(.width(32), .Select("low")) register_3 (.en(regd3), .Q(reg3), .clk(in_1));  // open: D, clr
  Register #(.width(32), .Select("low")) register_4 (.D(DATA), .en(regd4), .Q(reg4), .clk(in_1));  // open: clr
  Register #(.width(32), .Select("low")) register_5 (.D(DATA), .en(regd5), .Q(reg5), .clk(in_1));  // open: clr
  Register #(.width(32), .Select("low")) register_6 (.D(DATA), .en(regd6), .Q(reg6), .clk(in_1));  // open: clr
  Register #(.width(32), .Select("low")) register_7 (.D(DATA), .en(regd7), .Q(reg7), .clk(in_1));  // open: clr
  Register #(.width(32), .Select("low")) register_8 (.D(DATA), .en(regd8), .Q(reg8), .clk(in_1));  // open: clr
  Register #(.width(32), .Select("low")) register_9 (.D(DATA), .en(regd9), .Q(reg9), .clk(in_1));  // open: clr
  Register #(.width(32), .Select("low")) register_10 (.D(DATA), .en(regd10), .Q(reg10), .clk(in_1));  // open: clr
  Register #(.width(32), .Select("low")) register_11 (.D(DATA), .en(regd11), .Q(reg11), .clk(in_1));  // open: clr
  Register #(.width(32), .Select("low")) register_12 (.D(DATA), .en(regd12), .Q(reg12), .clk(in_1));  // open: clr
  Register #(.width(32), .Select("low")) register_13 (.D(DATA), .en(regd13), .Q(reg13), .clk(in_1));  // open: clr
  Register #(.width(32), .Select("low")) register_14 (.D(DATA), .en(regd14), .Q(reg14), .clk(in_1));  // open: clr
  Register #(.width(32), .Select("low")) register_15 (.D(DATA), .en(regd15), .Q(reg15), .clk(in_1));  // open: clr
  Register #(.width(32), .Select("low")) register_16 (.D(DATA), .en(regd16), .Q(reg16), .clk(in_1));  // open: clr
  Register #(.width(32), .Select("low")) register_17 (.D(DATA), .en(regd17), .Q(reg17), .clk(in_1));  // open: clr
  Register #(.width(32), .Select("low")) register_18 (.D(DATA), .en(regd18), .Q(reg18), .clk(in_1));  // open: clr
  Register #(.width(32), .Select("low")) register_19 (.D(DATA), .en(regd19), .Q(reg19), .clk(in_1));  // open: clr
  Register #(.width(32), .Select("low")) register_20 (.D(DATA), .en(regd20), .Q(reg20), .clk(in_1));  // open: clr
  Register #(.width(32), .Select("low")) register_21 (.D(DATA), .en(regd21), .Q(reg21), .clk(in_1));  // open: clr
  Register #(.width(32), .Select("low")) register_22 (.D(DATA), .en(regd22), .Q(reg22), .clk(in_1));  // open: clr
  Register #(.width(32), .Select("low")) register_23 (.D(DATA), .en(regd23), .Q(reg23), .clk(in_1));  // open: clr
  Register #(.width(32), .Select("low")) register_24 (.D(DATA), .en(regd24), .Q(reg24), .clk(in_1));  // open: clr
  Register #(.width(32), .Select("low")) register_25 (.D(DATA), .en(regd25), .Q(reg25), .clk(in_1));  // open: clr
  Register #(.width(32), .Select("low")) register_26 (.D(DATA), .en(regd26), .Q(reg26), .clk(in_1));  // open: clr
  Register #(.width(32), .Select("low")) register_27 (.D(DATA), .en(regd27), .Q(reg27), .clk(in_1));  // open: clr
  Register #(.width(32), .Select("low")) register_28 (.D(DATA), .en(regd28), .Q(reg28), .clk(in_1));  // open: clr
  Register #(.width(32), .Select("low")) register_29 (.D(DATA), .en(regd29), .Q(reg29), .clk(in_1));  // open: clr
  Register #(.width(32), .Select("low")) register_30 (.D(DATA), .en(regd30), .Q(reg30), .clk(in_1));  // open: clr
  Register #(.width(32), .Select("low")) register_31 (.D(DATA), .en(regd31), .Q(reg31), .clk(in_1));  // open: clr
  Register #(.width(32), .Select("low")) register_32 (.D(DATA), .en(regd32), .Q(reg32), .clk(in_1));  // open: clr
  Multiplexer #(.select(5), .width(32), .enable("false")) multiplexer_1 (
    .in0(reg1), .in1(reg2), .in2(reg3), .in3(reg4), .in4(reg5), .in5(reg6), .in6(reg7), .in7(reg8),
    .in8(reg9), .in9(reg10), .in10(reg11), .in11(reg12), .in12(reg13), .in13(reg14), .in14(reg15),
    .in15(reg16), .in16(reg17), .in17(reg18), .in18(reg19), .in19(reg20), .in20(reg21), .in21(reg22),
    .in22(reg23), .in23(reg24), .in24(reg25), .in25(reg26), .in26(reg27), .in27(reg28), .in28(reg29),
    .in29(reg30), .in30(reg31), .in31(reg32), .out(BR_RS), .sel(RS));
  Multiplexer #(.select(5), .width(32), .enable("false")) multiplexer_2 (
    .in0(reg1), .in1(reg2), .in2(reg3), .in3(reg4), .in4(reg5), .in5(reg6), .in6(reg7), .in7(reg8),
    .in8(reg9), .in9(reg10), .in10(reg11), .in11(reg12), .in12(reg13), .in13(reg14), .in14(reg15),
    .in15(reg16), .in16(reg17), .in17(reg18), .in18(reg19), .in19(reg20), .in20(reg21), .in21(reg22),
    .in22(reg23), .in23(reg24), .in24(reg25), .in25(reg26), .in26(reg27), .in27(reg28), .in28(reg29),
    .in29(reg30), .in30(reg31), .in31(reg32), .out(BR_RT), .sel(RT));

  // Other names for the same wires on the sheet: clk = in_1
endmodule

module \ULA___Unidade_Lógica_e_Aritmetica  (
  input  [31:0] BR_RS,
  input  [2:0] ULA_OP,
  input  [31:0] BR_RT,
  input  [4:0] shamt,
  output Flag_beq,
  output [31:0] DATA,
  output slt
);

  wire [31:0] adder_1_out, bit_extender_1_out, divider_1_out, multiplier_1_out, shifter_1_out, shifter_2_out,
       subtractor_1_out;

  Comparator #(.width(32)) comparator_1 (.a(BR_RS), .b(BR_RT), .lt(slt));  // open: gt, eq
  Comparator #(.width(32)) comparator_2 (.a(BR_RS), .b(BR_RT), .eq(Flag_beq));  // open: gt, lt
  Adder #(.width(32)) adder_1 (.a(BR_RS), .b(BR_RT), .out(adder_1_out));  // open: cin, cout
  Subtractor #(.width(32)) subtractor_1 (.a(BR_RS), .b(BR_RT), .out(subtractor_1_out));  // open: bin, bout
  Multiplier #(.width(32)) multiplier_1 (.a(BR_RS), .b(BR_RT), .out(multiplier_1_out));  // open: cin, cout
  Divider #(.width(32)) divider_1 (.a(BR_RS), .b(BR_RT), .out(divider_1_out));  // open: upper, rem
  assign bit_extender_1_out = {{31{1'b0}}, slt};  // Bit_Extender bit_extender_1
  Shifter #(.width(32)) shifter_1 (.in(BR_RT), .\dist (shamt), .out(shifter_1_out));
  Shifter #(.width(32), .shift("lr")) shifter_2 (.in(BR_RT), .\dist (shamt), .out(shifter_2_out));
  Multiplexer #(.select(3), .width(32), .enable("false")) multiplexer_1 (
    .in0(adder_1_out), .in1(subtractor_1_out), .in2(multiplier_1_out), .in3(divider_1_out),
    .in4(bit_extender_1_out), .in5(shifter_1_out), .in6(shifter_2_out), .out(DATA), .sel(ULA_OP));  // open: in7
endmodule

module \MI___Memória_de_Instruções  (
  input  clock,
  output [31:0] Instruction
);

  wire [23:0] adder_1_out, PC___Programing_Counting_q;

  Adder #(.width(24)) adder_1 (.a(PC___Programing_Counting_q), .b(24'h1), .out(adder_1_out));  // open: cin, cout
  Register #(.width(24), .Select("low")) PC___Programing_Counting (
    .D(adder_1_out), .Q(PC___Programing_Counting_q), .clk(clock));  // open: en, clr
  RAM #(.addrWidth(24), .dataWidth(32), .Select("low")) ram_1 (
    .addr(PC___Programing_Counting_q), .data(Instruction));  // open: sel, clk, ld, clr
endmodule

module CU___Control_Unit (
  input  [31:0] Instruction,
  output Type_R,
  output selector_r_i,
  output lw,
  output sw,
  output Type_I,
  output beq,
  output addi,
  output [4:0] RD_R,
  output Type_J,
  output [5:0] FUNCT,
  output [4:0] SHANT,
  output [4:0] RT_R,
  output [4:0] RS_R,
  output [15:0] Imediate,
  output [4:0] RT_I,
  output [4:0] RS_I,
  output [25:0] Label
);

  wire comparator_6_eq, comparator_7_eq;

  Comparator #(.width(6)) comparator_1 (.a(Instruction[31:26]), .b({6{1'b0}}), .eq(Type_R));  // open: gt, lt
  Comparator #(.width(6)) comparator_2 (.a(Instruction[31:26]), .b(6'b100011), .eq(lw));  // open: gt, lt
  Comparator #(.width(6)) comparator_3 (.a(Instruction[31:26]), .b(6'b101011), .eq(sw));  // open: gt, lt
  Comparator #(.width(6)) comparator_4 (.a(Instruction[31:26]), .b(6'b000100), .eq(beq));  // open: gt, lt
  Comparator #(.width(6)) comparator_5 (.a(Instruction[31:26]), .b(6'b001000), .eq(addi));  // open: gt, lt
  Comparator #(.width(6)) comparator_6 (.a(Instruction[31:26]), .b(6'b000010), .eq(comparator_6_eq));  // open: gt, lt
  Comparator #(.width(6)) comparator_7 (.a(Instruction[31:26]), .b(6'b000011), .eq(comparator_7_eq));  // open: gt, lt
  or or_1 (Type_I, lw, sw, beq, addi);
  or or_2 (Type_J, comparator_6_eq, comparator_7_eq);
  or or_3 (selector_r_i, Type_R, addi, lw);

  assign FUNCT = Instruction[5:0];
  assign Imediate = Instruction[15:0];
  assign Label = Instruction[25:0];
  assign RD_R = Instruction[15:11];
  assign RS_I = Instruction[25:21];
  assign RS_R = Instruction[25:21];
  assign RT_I = Instruction[20:16];
  assign RT_R = Instruction[20:16];
  assign SHANT = Instruction[10:6];

  // Other names for the same wires on the sheet: remained[25:0] = Instruction[25:0]; opcode[5:0] = Instruction[31:26]
endmodule
